// Logisim project Codificador 1 Jokenpo.circ as structural Verilog: 1 circuit, main circuit main
module main (
  input  PEDRA,
  input  PAPEL,
  input  TESOURA,
  output S1,
  output S2,
  output S1_2,
  output S1_3
);

  wire and_1_out, and_2_out, and_3_out, and_4_out, xor_1_out, xor_2_out;

  and and_1 (and_1_out, ~PEDRA, ~PAPEL, TESOURA);  // AND_Gate
  and and_2 (and_2_out, ~PEDRA, PAPEL, ~TESOURA);  // AND_Gate
  and and_3 (and_3_out, ~PEDRA, ~PAPEL, TESOURA);  // AND_Gate
  and and_4 (and_4_out, PEDRA, ~PAPEL, ~TESOURA);  // AND_Gate
  xor xor_1 (xor_1_out, PAPEL, TESOURA);
  xor xor_2 (xor_2_out, PEDRA, TESOURA);
  or or_1 (S1, and_1_out, and_2_out);
  or or_2 (S2, and_3_out, and_4_out);
  and and_5 (S1_2, ~PEDRA, xor_1_out);  // AND_Gate
  and and_6 (S1_3, ~PAPEL, xor_2_out);  // AND_Gate

  // Notes on the sheet:
  //   PADRÃO
  //   SIMPLIFICADO
endmodule
